// Logisim project Lab 1 ALU - N.circ as structural Verilog: 7 circuits, main circuit Unit 3
module ALU (
  input  [3:0] A,
  input  [3:0] B,
  input  Mode,
  input  Control,
  input  R_W,
  output Overflow,
  output Carry_Out,
  output [3:0] C,
  output out_9,
  output out_10,
  output out_11,
  output out_12,
  output out_13,
  output out_14,
  output out_15,
  output out_16,
  output out_17,
  output out_18,
  output out_19,
  output out_20
);

  Unit_3 unit_3_1 (
    .in_1(A), .B(B), .Mode(Mode), .Control(Control), .C(C[3]), .out_8(C[2]), .out_9(C[1]), .out_10(C[0]),
    .Overflow(Overflow), .Carry_Out(Carry_Out));
  Unit_4 A_Register (
    .in_1(A[3]), .in_2(A[2]), .in_3(A[1]), .in_4(A[0]), .out_6(out_13), .out_7(out_14), .out_8(out_15),
    .out_9(out_16), .Clear_b(R_W));
  Unit_4 B_Register (
    .in_1(B[3]), .in_2(B[2]), .in_3(B[1]), .in_4(B[0]), .out_6(out_17), .out_7(out_18), .out_8(out_19),
    .out_9(out_20), .Clear_b(R_W));
  Unit_4 C_Register (
    .in_1(C[3]), .in_2(C[2]), .in_3(C[1]), .in_4(C[0]), .out_6(out_9), .out_7(out_10), .out_8(out_11),
    .out_9(out_12), .Clear_b(R_W));

  // Notes on the sheet:
  //   A/L
endmodule

module Unit_4 (
  input  in_1,
  input  in_2,
  input  in_3,
  input  in_4,
  input  Clear_b,
  output out_6,
  output out_7,
  output out_8,
  output out_9
);

  wire clock_1_out, not_1_out;

  Clock clock_1 (.out(clock_1_out));
  not not_1 (not_1_out, Clear_b);
  D_Flip_Flop d_ff_1 (.clk(clock_1_out), .D(in_1), .Q(out_6), .en(not_1_out));  // open: Qn, preset, reset
  D_Flip_Flop d_ff_2 (.clk(clock_1_out), .D(in_2), .Q(out_7), .en(not_1_out));  // open: Qn, preset, reset
  D_Flip_Flop d_ff_3 (.clk(clock_1_out), .D(in_3), .Q(out_8), .en(not_1_out));  // open: Qn, preset, reset
  D_Flip_Flop d_ff_4 (.clk(clock_1_out), .D(in_4), .Q(out_9), .en(not_1_out));  // open: Qn, preset, reset

  // Notes on the sheet:
  //   Clk
  //   1
  //   2
  //   3
  //   4
endmodule

// ALU
module Unit_3 (
  input  [3:0] in_1,
  input  [3:0] B,
  input  Mode,
  input  Control,
  output Overflow,
  output Carry_Out,
  output C,
  output out_8,
  output out_9,
  output out_10
);

  wire unit_1_1_s0, unit_1_1_s1, unit_1_1_s2, unit_1_1_s3, unit_2_1_c, unit_2_1_out_5, unit_2_1_out_6,
       unit_2_1_out_7;

  Unit_1 unit_1_1 (
    .Cout(Carry_Out), .Overflow(Overflow), .Cin(Mode), .B3(B[0]), .A3(in_1[0]), .B2(B[1]), .A2(in_1[1]),
    .B1(B[2]), .A1(in_1[2]), .B0(B[3]), .A0(in_1[3]), .S3(unit_1_1_s3), .S2(unit_1_1_s2), .S1(unit_1_1_s1),
    .S0(unit_1_1_s0));
  Unit_2 unit_2_1 (
    .in_1(in_1), .in_2(B), .in_3(Mode), .C(unit_2_1_c), .out_5(unit_2_1_out_5), .out_6(unit_2_1_out_6),
    .out_7(unit_2_1_out_7));
  _8x4_MUX u_8x4_mux_1 (
    .in_1(unit_1_1_s0), .in_2(unit_1_1_s1), .in_3(unit_1_1_s2), .in_4(unit_1_1_s3), .in_5(unit_2_1_c),
    .in_6(unit_2_1_out_5), .in_7(unit_2_1_out_6), .in_8(unit_2_1_out_7), .in_9(Control), .out_10(C),
    .out_11(out_8), .out_12(out_9), .out_13(out_10));

  // Notes on the sheet:
  //   A
endmodule

module Unit_2 (
  input  [3:0] in_1,
  input  [3:0] in_2,
  input  in_3,
  output C,
  output out_5,
  output out_6,
  output out_7
);

  wire [3:0] and_1_out, or_1_out;

  assign and_1_out = in_1 & in_2;  // AND_Gate and_1, 4 bits wide
  assign or_1_out = in_1 | in_2;  // OR_Gate or_1, 4 bits wide
  _8x4_MUX u_8x4_mux_1 (
    .in_1(and_1_out[3]), .in_2(and_1_out[2]), .in_3(and_1_out[1]), .in_4(and_1_out[0]), .in_5(or_1_out[3]),
    .in_6(or_1_out[2]), .in_7(or_1_out[1]), .in_8(or_1_out[0]), .in_9(in_3), .out_10(C), .out_11(out_5),
    .out_12(out_6), .out_13(out_7));
endmodule

module Unit_1 (
  input  B2,
  input  A2,
  input  B1,
  input  A1,
  input  B0,
  input  A0,
  input  B3,
  input  A3,
  input  Cin,
  output Cout,
  output Overflow,
  output S3,
  output S2,
  output S1,
  output S0
);

  wire full_adder_2_cout, full_adder_3_cout, full_adder_4_cout, xor_2_out, xor_3_out, xor_4_out, xor_5_out;

  xor xor_1 (Overflow, Cout, full_adder_2_cout);
  xor xor_2 (xor_2_out, Cin, B3);
  Full_Adder full_adder_1 (.A(A3), .B(xor_2_out), .Cin(full_adder_2_cout), .S(S3), .Cout(Cout));
  xor xor_3 (xor_3_out, Cin, B2);
  Full_Adder full_adder_2 (.A(A2), .B(xor_3_out), .Cin(full_adder_3_cout), .S(S2), .Cout(full_adder_2_cout));
  xor xor_4 (xor_4_out, Cin, B1);
  Full_Adder full_adder_3 (.A(A1), .B(xor_4_out), .Cin(full_adder_4_cout), .S(S1), .Cout(full_adder_3_cout));
  xor xor_5 (xor_5_out, Cin, B0);
  Full_Adder full_adder_4 (.A(A0), .B(xor_5_out), .Cin(Cin), .S(S0), .Cout(full_adder_4_cout));
endmodule

module Full_Adder (
  input  A,
  input  B,
  input  Cin,
  output S,
  output Cout
);

  wire and_1_out, and_2_out, xor_1_out;

  xor xor_1 (xor_1_out, A, B);
  and and_1 (and_1_out, A, B);
  xor xor_2 (S, xor_1_out, Cin);
  and and_2 (and_2_out, Cin, xor_1_out);
  or or_1 (Cout, and_2_out, and_1_out);
endmodule

// MUX
module _8x4_MUX (
  input  in_1,
  input  in_2,
  input  in_3,
  input  in_4,
  input  in_5,
  input  in_6,
  input  in_7,
  input  in_8,
  input  in_9,
  output out_10,
  output out_11,
  output out_12,
  output out_13
);

  wire and_1_out, and_2_out, and_3_out, and_4_out, and_5_out, and_6_out, and_7_out, and_8_out, not_1_out,
       not_2_out;

  not not_1 (not_1_out, in_9);
  not not_2 (not_2_out, not_1_out);
  and and_1 (and_1_out, in_1, not_1_out);
  and and_2 (and_2_out, in_2, not_1_out);
  and and_3 (and_3_out, in_3, not_1_out);
  and and_4 (and_4_out, in_4, not_1_out);
  and and_5 (and_5_out, in_5, not_2_out);
  and and_6 (and_6_out, in_6, not_2_out);
  and and_7 (and_7_out, in_7, not_2_out);
  and and_8 (and_8_out, in_8, not_2_out);
  or or_1 (out_10, and_1_out, and_5_out);
  or or_2 (out_11, and_2_out, and_6_out);
  or or_3 (out_12, and_3_out, and_7_out);
  or or_4 (out_13, and_4_out, and_8_out);
endmodule
